# Fritzing sketch incubator (saved by Fritzing 0.9.3b)
breadboards: 1

parts:
  Part1 = Arduino Uno (Rev3) - ICSP
  DHT1 = Humidity and Temperature Sensor DHT11
  Part2 = LCD1602-I2C
  U1 = POT [package=pot_mammoth]
  KY-1 = Keyes Relay [package=THT]
  Power_plug1 = Power plug
  J1 = Peltier Element
  S1 = Momentary Switch [package=ksa_sealed_tac_switch]

nets:
  N1: Part1.A0, U1.A
  N2: Part1.A4/SDA, Part2.SDA
  N3: Part1.A5/SCL, Part2.SCL
  N4: Part1.D8, S1.3
  N5: Part1.D9_PWM, KY-1.signal
  N6: Part1.D2, DHT1.Data-signal
  VCC: Part1.5V, DHT1.Vcc, Part2.VCC, U1.E, KY-1.power
  GND: Part1.GND, DHT1.GND_2, Part2.GND, U1.S, KY-1.ground, S1.1
  N7: KY-1.C, J1.pin2
  N8: KY-1.NO, Power_plug1.VCC
  N9: Power_plug1.GND, J1.pin1

notes:
  We replaced peltier element with 75W incandescent bulb capable of producing large amounts of heat in a short time.
  A slide potentiometer can also be used.

custom parts:
  Humidity and Temperature Sensor DHT11: Digital relative humidity & temperature sensor DHT11
  LCD1602-I2C: A standard character display, usually with 2x16 characters. Comes in many colors with LCM1602 IIC attached.
  Keyes Relay: The Keyes 5V relay module is suitable for SCM development, home appliance control. It uses a 5V~12V TIL control signal which can control DC / AC signal.
